// Logisim project Lab3.circ as structural Verilog: 7 circuits, main circuit Main
module Main (
  output [3:0] out_1
);

  wire ALUSrcA, and_1_out, Branch, Clock, IorD, IRWrite, Jal, Jr, Jump, MemRead, MemWr, or_1_out, PCWrite,
       PCWriteCond, RegWrite, Zero;
  wire [1:0] ALUSrcB_0_1, MemtoReg_0_1, PCSource_0_1, RegDst_0_1;
  wire [3:0] ALUOp, NextState, State;
  wire [4:0] WrAddr;
  wire [5:0] func;
  wire [7:0] ALU_128, multiplexer_1_out;
  wire [27:0] adder_2_out;
  wire [31:0] A, alu_1_aluresult, ALUout, B, MDR, multiplexer_4_out, multiplexer_5_out, multiplexer_6_out,
       PC, ram_1_data, register_file_1_rddata1, register_file_1_rddata2, Sign_Extend, SignExtShifted, WrData;
  wire [31:2] RightMux2;
  wire [31:6] IR;

  Clock u_Clock (.out(Clock));
  and and_1 (and_1_out, Zero, PCWriteCond);
  or or_1 (or_1_out, PCWrite, and_1_out);
  Adder adder_1 (.a(ALUout[7:0]), .b(8'h80), .out(ALU_128));  // open: cin, cout
  Adder #(.width(32)) adder_2 (.a(PC), .b(32'h4), .out({RightMux2[31:28], adder_2_out}));  // open: cin, cout
  Register #(.width(32)) u_PC (.D(multiplexer_6_out), .en(or_1_out), .Q(PC), .clk(Clock));  // open: clr
  Control_Unit control_unit_1 (
    .op5(IR[31]), .op4(IR[30]), .op3(IR[29]), .op2(IR[28]), .op1(IR[27]), .op0(IR[26]), .s3(State[3]),
    .s2(State[2]), .s1(State[1]), .s0(State[0]), .NS3(NextState[3]), .NS2(NextState[2]), .NS1(NextState[1]),
    .NS0(NextState[0]), .PCWrite(PCWrite), .PCWriteCond(PCWriteCond), .IorD(IorD), .MemRead(MemRead),
    .MemWrite(MemWr), .IRWrite(IRWrite), .MemtoReg1(MemtoReg_0_1[1]), .MemtoReg0(MemtoReg_0_1[0]),
    .PCSource1(PCSource_0_1[1]), .PCSource0(PCSource_0_1[0]), .ALUOp3(ALUOp[3]), .ALUOp2(ALUOp[2]),
    .ALUOp1(ALUOp[1]), .ALUOp0(ALUOp[0]), .ALUSrcB1(ALUSrcB_0_1[1]), .ALUSrcB0(ALUSrcB_0_1[0]),
    .ALUSrcA(ALUSrcA), .RegWrite(RegWrite), .RegDst1(RegDst_0_1[1]), .RegDst0(RegDst_0_1[0]), .Clock(Clock));
  Multiplexer #(.width(8), .enable("false")) multiplexer_1 (
    .in0(PC[9:2]), .in1(ALUout[9:2]), .out(multiplexer_1_out), .sel(IorD));
  Shifter #(.width(26)) shifter_1 (.in({IR[25:6], func}), .\dist (5'b00010), .out(RightMux2[27:2]));
  RAM #(.dataWidth(32), .bus("separate")) ram_1 (
    .addr(multiplexer_1_out), .din(B), .data(ram_1_data), .str(MemWr), .clk(Clock), .ld(MemRead));  // open: sel, clr
  Register #(.width(32)) u_IR (.D(ram_1_data), .en(IRWrite), .Q({IR, func}), .clk(Clock));  // open: clr
  Register #(.width(32)) u_MDR (.D(ram_1_data), .Q(MDR), .clk(Clock));  // open: en, clr
  Multiplexer #(.select(2), .width(5), .enable("false")) multiplexer_2 (
    .in0(IR[20:16]), .in1(IR[15:11]), .in2({5{1'b1}}), .out(WrAddr), .sel(RegDst_0_1));  // open: in3
  Multiplexer #(.select(2), .width(32), .enable("false")) multiplexer_3 (
    .in0(ALUout), .in1(MDR), .in2(PC), .out(WrData), .sel(MemtoReg_0_1));  // open: in3
  assign Sign_Extend = {{16{1'b0}}, {IR[15:6], func}};  // Bit_Extender bit_extender_1
  Register_File register_file_1 (
    .WrAddr(WrAddr), .WrData(WrData), .WrReg(RegWrite), .RdAddr1(IR[25:21]), .RdAddr2(IR[20:16]),
    .RdData1(register_file_1_rddata1), .RdData2(register_file_1_rddata2), .Clock(Clock));
  Register #(.width(32)) u_A (.D(register_file_1_rddata1), .Q(A), .clk(Clock));  // open: en, clr
  Register #(.width(32)) u_B (.D(register_file_1_rddata2), .Q(B), .clk(Clock));  // open: en, clr
  Shifter #(.width(32)) shifter_2 (.in(Sign_Extend), .\dist (5'b00010), .out(SignExtShifted));
  Multiplexer #(.width(32), .enable("false")) multiplexer_4 (.in0(PC), .in1(A), .out(multiplexer_4_out), .sel(ALUSrcA));
  Multiplexer #(.select(2), .width(32), .enable("false")) multiplexer_5 (
    .in0(B), .in1(32'h4), .in2(Sign_Extend), .in3(SignExtShifted), .out(multiplexer_5_out), .sel(ALUSrcB_0_1));
  ALU alu_1 (
    .ALUCtl(out_1), .A(multiplexer_4_out), .B(multiplexer_5_out), .ALUResult(alu_1_aluresult), .Zero(Zero),
    .Shamt(IR[10:6]));  // open: Overflow
  Multiplexer #(.select(2), .width(32), .enable("false")) multiplexer_6 (
    .in0(alu_1_aluresult), .in1(ALUout), .in2({RightMux2, 2'b00}), .out(multiplexer_6_out), .sel(PCSource_0_1));  // open: in3
  Register #(.width(32)) u_ALUout (.D(alu_1_aluresult), .Q(ALUout), .clk(Clock));  // open: en, clr
  ALUControl alucontrol_1 (
    .ALUOp3(ALUOp[3]), .ALUOp2(ALUOp[2]), .ALUOp1(ALUOp[1]), .ALUOp0(ALUOp[0]), .func5(func[5]),
    .func4(func[4]), .func3(func[3]), .func2(func[2]), .func1(func[1]), .func0(func[0]), .ALUCtl3(out_1[3]),
    .ALUCtl2(out_1[2]), .ALUCtl1(out_1[1]), .ALUCtl0(out_1[0]));
  // Probe on PC
  // Probe on Branch
  // Probe on Jump
  // Probe on Jal
  // Probe on Jr
  // Probe on RegWrite
  // Probe on WrAddr
  // Probe on WrData
  // Probe on MemWr
  // Probe on B

  // Other names for the same wires on the sheet: IR[5:0] = func; shamt[4:0] = IR[10:6]; rd[4:0] = IR[15:11];
  //   ALUCtl[3:0] = out_1; rt[4:0] = IR[20:16]; rs[4:0] = IR[25:21]; op[5:0] = IR[31:26]; MemData[31:0] = B
endmodule

module ALU (
  input  [3:0] ALUCtl,
  input  [31:0] A,
  input  [31:0] B,
  input  [4:0] Shamt,
  output [31:0] ALUResult,
  output Zero,
  output Overflow
);

  wire comparator_1_lt, comparator_2_lt, comparator_3_eq, comparator_4_eq, or_2_out;
  wire [31:0] ADD, AND, NOR, OR, SLL, SLT, SLTU, SRL, SUB, XOR;

  // Probe on ALUCtl
  assign NOR = ~(A | B);  // NOR_Gate nor_1, 32 bits wide
  Adder #(.width(32)) adder_1 (.a(A), .b(B), .out(ADD));  // open: cin, cout
  Subtractor #(.width(32)) subtractor_1 (.a(A), .b(B), .out(SUB));  // open: bin, bout
  assign AND = A & B;  // AND_Gate and_1, 32 bits wide
  assign OR = A | B;  // OR_Gate or_1, 32 bits wide
  assign XOR = A ^ B;  // XOR_Gate xor_1, 32 bits wide
  Comparator #(.width(32)) comparator_1 (.a(A), .b(B), .lt(comparator_1_lt));  // open: gt, eq
  assign SLT = {{31{1'b0}}, comparator_1_lt};  // Bit_Extender bit_extender_1
  Shifter #(.width(32)) shifter_1 (.in(B), .\dist (Shamt), .out(SLL));
  Shifter #(.width(32), .shift("lr")) shifter_2 (.in(B), .\dist (Shamt), .out(SRL));
  Comparator #(.width(32), .mode("unsigned")) comparator_2 (.a(A), .b(B), .lt(comparator_2_lt));  // open: gt, eq
  assign SLTU = {{31{1'b0}}, comparator_2_lt};  // Bit_Extender bit_extender_2
  Multiplexer #(.select(4), .width(32), .enable("false")) multiplexer_1 (
    .in0(XOR), .in1(SLTU), .in2(SLT), .in3(AND), .in4(NOR), .in5(SUB), .in6(OR), .in7(ADD), .in8(SRL),
    .in9(SLL), .out(ALUResult), .sel(ALUCtl));  // open: in10, in11, in12, in13, in14, in15
  Comparator #(.width(4)) comparator_3 (.a(4'b0111), .b(ALUCtl), .eq(comparator_3_eq));  // open: gt, lt
  Comparator #(.width(4)) comparator_4 (.a(ALUCtl), .b(4'b0101), .eq(comparator_4_eq));  // open: gt, lt
  Overflow_Unit overflow_unit_1 (
    .Add(comparator_3_eq), .Sub(comparator_4_eq), .ASign(A[31]), .BSign(B[31]), .ResultSign(ALUResult[31]),
    .Overflow(Overflow));
  or or_2 (or_2_out, ALUResult[0], ALUResult[1], ALUResult[2], ALUResult[3], ALUResult[4], ALUResult[5], ALUResult[6], ALUResult[7], ALUResult[8], ALUResult[9], ALUResult[10], ALUResult[11], ALUResult[12], ALUResult[13], ALUResult[14], ALUResult[15], ALUResult[16], ALUResult[17], ALUResult[18], ALUResult[19], ALUResult[20], ALUResult[21], ALUResult[22], ALUResult[23], ALUResult[24], ALUResult[25], ALUResult[26], ALUResult[27], ALUResult[28], ALUResult[29], ALUResult[30], ALUResult[31]);
  not not_1 (Zero, or_2_out);

  // Other names for the same wires on the sheet: ASign = A[31]; ResultSign = ALUResult[31]; BSign = B[31]

  // Notes on the sheet:
  //   ALUCtl for ADD for top port
  //   ALUCtl for SUB for second port
endmodule

module Register_File (
  input  [4:0] WrAddr,
  input  [31:0] WrData,
  input  WrReg,
  input  [4:0] RdAddr1,
  input  [4:0] RdAddr2,
  input  Clock,
  output [31:0] RdData1,
  output [31:0] RdData2
);

  wire WrReg0, WrReg1, WrReg2, WrReg3, WrReg4, WrReg5, WrReg6, WrReg7, WrReg8, WrReg9, WrReg10, WrReg11,
       WrReg12, WrReg13, WrReg14, WrReg15, WrReg16, WrReg17, WrReg18, WrReg19, WrReg20, WrReg21, WrReg22,
       WrReg23, WrReg24, WrReg25, WrReg26, WrReg27, WrReg28, WrReg29, WrReg30, WrReg31;
  wire [31:0] RegData1, RegData2, RegData3, RegData4, RegData5, RegData6, RegData7, RegData8, RegData9,
       RegData10, RegData11, RegData12, RegData13, RegData14, RegData15, RegData16, RegData17, RegData18,
       RegData19, RegData20, RegData21, RegData22, RegData23, RegData24, RegData25, RegData26, RegData27,
       RegData28, RegData29, RegData30, RegData31;

  Demultiplexer #(.select(5), .enable("false")) demultiplexer_1 (
    .out0(WrReg0), .out1(WrReg1), .out2(WrReg2), .out3(WrReg3), .out4(WrReg4), .out5(WrReg5), .out6(WrReg6),
    .out7(WrReg7), .out8(WrReg8), .out9(WrReg9), .out10(WrReg10), .out11(WrReg11), .out12(WrReg12),
    .out13(WrReg13), .out14(WrReg14), .out15(WrReg15), .out16(WrReg16), .out17(WrReg17), .out18(WrReg18),
    .out19(WrReg19), .out20(WrReg20), .out21(WrReg21), .out22(WrReg22), .out23(WrReg23), .out24(WrReg24),
    .out25(WrReg25), .out26(WrReg26), .out27(WrReg27), .out28(WrReg28), .out29(WrReg29), .out30(WrReg30),
    .out31(WrReg31), .in(WrReg), .sel(WrAddr));
  // Probe on RegData4
  Register #(.width(32)) Reg4 (.D(WrData), .en(WrReg4), .Q(RegData4), .clk(Clock));  // open: clr
  // Probe on RegData8
  Register #(.width(32)) Reg8 (.D(WrData), .en(WrReg8), .Q(RegData8), .clk(Clock));  // open: clr
  // Probe on RegData12
  Register #(.width(32)) Reg12 (.D(WrData), .en(WrReg12), .Q(RegData12), .clk(Clock));  // open: clr
  // Probe on RegData16
  Register #(.width(32)) Reg16 (.D(WrData), .en(WrReg16), .Q(RegData16), .clk(Clock));  // open: clr
  // Probe on RegData20
  Register #(.width(32)) Reg20 (.D(WrData), .en(WrReg20), .Q(RegData20), .clk(Clock));  // open: clr
  // Probe on RegData24
  Register #(.width(32)) Reg24 (.D(WrData), .en(WrReg24), .Q(RegData24), .clk(Clock));  // open: clr
  // Probe on RegData28
  Register #(.width(32)) Reg28 (.D(WrData), .en(WrReg28), .Q(RegData28), .clk(Clock));  // open: clr
  Register #(.width(32)) Reg1 (.D(WrData), .en(WrReg1), .Q(RegData1), .clk(Clock));  // open: clr
  Register #(.width(32)) Reg5 (.D(WrData), .en(WrReg5), .Q(RegData5), .clk(Clock));  // open: clr
  Register #(.width(32)) Reg9 (.D(WrData), .en(WrReg9), .Q(RegData9), .clk(Clock));  // open: clr
  Register #(.width(32)) Reg13 (.D(WrData), .en(WrReg13), .Q(RegData13), .clk(Clock));  // open: clr
  Register #(.width(32)) Reg17 (.D(WrData), .en(WrReg17), .Q(RegData17), .clk(Clock));  // open: clr
  Register #(.width(32)) Reg21 (.D(WrData), .en(WrReg21), .Q(RegData21), .clk(Clock));  // open: clr
  Register #(.width(32)) Reg25 (.D(WrData), .en(WrReg25), .Q(RegData25), .clk(Clock));  // open: clr
  Register #(.width(32)) Reg29 (.D(WrData), .en(WrReg29), .Q(RegData29), .clk(Clock));  // open: clr
  // Probe on RegData1
  // Probe on RegData5
  // Probe on RegData9
  // Probe on RegData13
  // Probe on RegData17
  // Probe on RegData21
  // Probe on RegData25
  // Probe on RegData29
  // Probe on RegData2
  Register #(.width(32)) Reg2 (.D(WrData), .en(WrReg2), .Q(RegData2), .clk(Clock));  // open: clr
  // Probe on RegData6
  Register #(.width(32)) Reg6 (.D(WrData), .en(WrReg6), .Q(RegData6), .clk(Clock));  // open: clr
  // Probe on RegData10
  Register #(.width(32)) Reg10 (.D(WrData), .en(WrReg10), .Q(RegData10), .clk(Clock));  // open: clr
  // Probe on RegData14
  Register #(.width(32)) Reg14 (.D(WrData), .en(WrReg14), .Q(RegData14), .clk(Clock));  // open: clr
  // Probe on RegData18
  Register #(.width(32)) Reg18 (.D(WrData), .en(WrReg18), .Q(RegData18), .clk(Clock));  // open: clr
  // Probe on RegData22
  Register #(.width(32)) Reg22 (.D(WrData), .en(WrReg22), .Q(RegData22), .clk(Clock));  // open: clr
  // Probe on RegData26
  Register #(.width(32)) Reg26 (.D(WrData), .en(WrReg26), .Q(RegData26), .clk(Clock));  // open: clr
  // Probe on RegData30
  Register #(.width(32)) Reg30 (.D(WrData), .en(WrReg30), .Q(RegData30), .clk(Clock));  // open: clr
  // Probe on RegData3
  Register #(.width(32)) Reg3 (.D(WrData), .en(WrReg3), .Q(RegData3), .clk(Clock));  // open: clr
  // Probe on RegData7
  Register #(.width(32)) Reg7 (.D(WrData), .en(WrReg7), .Q(RegData7), .clk(Clock));  // open: clr
  // Probe on RegData11
  Register #(.width(32)) Reg11 (.D(WrData), .en(WrReg11), .Q(RegData11), .clk(Clock));  // open: clr
  // Probe on RegData15
  Register #(.width(32)) Reg15 (.D(WrData), .en(WrReg15), .Q(RegData15), .clk(Clock));  // open: clr
  // Probe on RegData19
  Register #(.width(32)) Reg19 (.D(WrData), .en(WrReg19), .Q(RegData19), .clk(Clock));  // open: clr
  // Probe on RegData23
  Register #(.width(32)) Reg23 (.D(WrData), .en(WrReg23), .Q(RegData23), .clk(Clock));  // open: clr
  // Probe on RegData27
  Register #(.width(32)) Reg27 (.D(WrData), .en(WrReg27), .Q(RegData27), .clk(Clock));  // open: clr
  // Probe on RegData31
  Register #(.width(32)) Reg31 (.D(WrData), .en(WrReg31), .Q(RegData31), .clk(Clock));  // open: clr
  Multiplexer #(.select(5), .width(32), .enable("false")) multiplexer_1 (
    .in0({32{1'b0}}), .in1(RegData1), .in2(RegData2), .in3(RegData3), .in4(RegData4), .in5(RegData5),
    .in6(RegData6), .in7(RegData7), .in8(RegData8), .in9(RegData9), .in10(RegData10), .in11(RegData11),
    .in12(RegData12), .in13(RegData13), .in14(RegData14), .in15(RegData15), .in16(RegData16),
    .in17(RegData17), .in18(RegData18), .in19(RegData19), .in20(RegData20), .in21(RegData21),
    .in22(RegData22), .in23(RegData23), .in24(RegData24), .in25(RegData25), .in26(RegData26),
    .in27(RegData27), .in28(RegData28), .in29(RegData29), .in30(RegData30), .in31(RegData31), .out(RdData1),
    .sel(RdAddr1));
  Multiplexer #(.select(5), .width(32), .enable("false")) multiplexer_2 (
    .in0({32{1'b0}}), .in1(RegData1), .in2(RegData2), .in3(RegData3), .in4(RegData4), .in5(RegData5),
    .in6(RegData6), .in7(RegData7), .in8(RegData8), .in9(RegData9), .in10(RegData10), .in11(RegData11),
    .in12(RegData12), .in13(RegData13), .in14(RegData14), .in15(RegData15), .in16(RegData16),
    .in17(RegData17), .in18(RegData18), .in19(RegData19), .in20(RegData20), .in21(RegData21),
    .in22(RegData22), .in23(RegData23), .in24(RegData24), .in25(RegData25), .in26(RegData26),
    .in27(RegData27), .in28(RegData28), .in29(RegData29), .in30(RegData30), .in31(RegData31), .out(RdData2),
    .sel(RdAddr2));
endmodule

module Overflow_Unit (
  input  Add,
  input  Sub,
  input  ASign,
  input  BSign,
  input  ResultSign,
  output Overflow
);

  wire and_1_out, and_2_out, or_1_out, xnor_1_out, xor_1_out, xor_2_out;

  xnor xnor_1 (xnor_1_out, ASign, BSign);
  xor xor_1 (xor_1_out, ASign, BSign);
  and and_1 (and_1_out, xnor_1_out, Add);
  and and_2 (and_2_out, xor_1_out, Sub);
  or or_1 (or_1_out, and_1_out, and_2_out);
  xor xor_2 (xor_2_out, ResultSign, ASign);
  and and_3 (Overflow, or_1_out, xor_2_out);

  // Notes on the sheet:
  //   Overflow occurs when doing addition and sign(A) == sign(B) && sign(result) != sign(A)
  //   Or
  //   Overflow occurs when doing subtraction and sign(A) != sign(B) && sign(result) != sign(A)
endmodule

module Control_Unit (
  input  op5,
  input  op4,
  input  op3,
  input  op2,
  input  op1,
  input  op0,
  input  s3,
  input  s2,
  input  s1,
  input  s0,
  input  Clock,
  output PCWrite,
  output PCWriteCond,
  output IorD,
  output MemRead,
  output MemWrite,
  output IRWrite,
  output MemtoReg1,
  output MemtoReg0,
  output PCSource1,
  output PCSource0,
  output ALUOp3,
  output ALUOp2,
  output ALUOp1,
  output ALUOp0,
  output ALUSrcB1,
  output ALUSrcB0,
  output ALUSrcA,
  output RegWrite,
  output RegDst1,
  output RegDst0,
  output NS3,
  output NS2,
  output NS1,
  output NS0
);

  wire not_1_out, not_2_out, not_3_out, not_4_out, not_5_out, not_6_out, not_7_out, not_8_out, not_9_out,
       not_10_out;
  wire [1:0] AddrCtrl;
  wire [3:0] adder_1_out, rom_1_data, rom_2_data, State;

  not not_1 (not_1_out, op5);
  not not_2 (not_2_out, op4);
  not not_3 (not_3_out, op3);
  not not_4 (not_4_out, op2);
  not not_5 (not_5_out, op1);
  not not_6 (not_6_out, op0);
  not not_7 (not_7_out, s3);
  not not_8 (not_8_out, s2);
  not not_9 (not_9_out, s1);
  not not_10 (not_10_out, s0);
  // Probe on {op5, op4, op3, op2, op1, op0}
  // Probe on State
  Register #(.width(4)) u_State (.D({NS3, NS2, NS1, NS0}), .Q(State), .clk(Clock));  // open: en, clr
  ROM #(.addrWidth(6), .dataWidth(4)) rom_1 (.addr({op5, op4, op3, op2, op1, op0}), .data(rom_1_data));  // open: sel
  ROM #(.addrWidth(6), .dataWidth(4)) rom_2 (.addr({op5, op4, op3, op2, op1, op0}), .data(rom_2_data));  // open: sel
  Adder #(.width(4)) adder_1 (.a(4'b0001), .b(State), .out(adder_1_out));  // open: cin, cout
  Multiplexer #(.select(2), .width(4)) multiplexer_1 (
    .in0(4'b0000), .in1(rom_1_data), .in2(rom_2_data), .in3(adder_1_out), .out({NS3, NS2, NS1, NS0}),
    .sel(AddrCtrl));  // open: en
  ROM #(.addrWidth(4), .dataWidth(2)) rom_3 (.addr(State), .data(AddrCtrl));  // open: sel
  ROM #(.addrWidth(4), .dataWidth(20)) rom_4 (
    .addr(State),
    .data({PCWrite, PCWriteCond, IorD, MemRead, MemWrite, IRWrite, MemtoReg1, MemtoReg0, PCSource1, PCSource0, ALUOp3, ALUOp2, ALUOp1, ALUOp0, ALUSrcB1, ALUSrcB0, ALUSrcA, RegWrite, RegDst1, RegDst0}));  // open: sel

  // Other names for the same wires on the sheet: NextState[3:0] = {NS3, NS2, NS1, NS0}

  // Notes on the sheet:
  //   Dispatch ROM 1
  //   Dispatch ROM 2
  //   contents of rom_1 (hex, n*v repeats v):
  //   6 0 9 0 8 30*0 2 7*0 2
  //   contents of rom_2 (hex, n*v repeats v):
  //   35*0 3 7*0 5
  //   contents of rom_3 (hex, n*v repeats v):
  //   3 1 2 3 0 0 3
  //   contents of rom_4 (hex, n*v repeats v):
  //   94090 30 28 30000 1004 5*0 e8 4
  //   ALL OUTPUTS
endmodule

module ALUControl (
  input  ALUOp3,
  input  ALUOp2,
  input  ALUOp1,
  input  ALUOp0,
  input  func5,
  input  func4,
  input  func3,
  input  func2,
  input  func1,
  input  func0,
  output ALUCtl3,
  output ALUCtl2,
  output ALUCtl1,
  output ALUCtl0
);

  wire and_1_out, and_2_out, and_3_out, and_4_out, and_5_out, and_6_out, and_7_out, and_8_out, and_9_out,
       and_10_out, and_11_out, and_12_out, and_13_out, and_14_out, and_15_out, and_16_out, and_17_out,
       not_1_out, not_2_out, not_3_out, not_4_out, not_5_out, not_6_out, not_7_out, not_8_out, not_9_out,
       not_10_out, not_11_out, not_12_out, not_13_out, not_14_out, not_15_out, not_16_out, not_17_out,
       not_18_out, not_19_out, not_20_out, not_21_out, not_22_out, not_23_out, not_24_out, not_25_out,
       not_26_out, not_27_out, not_28_out, not_29_out, not_30_out, not_31_out;

  and and_1 (and_1_out, ALUOp2, ALUOp1, ALUOp0);
  not not_1 (not_1_out, ALUOp3);
  not not_2 (not_2_out, ALUOp2);
  not not_3 (not_3_out, ALUOp1);
  not not_4 (not_4_out, ALUOp3);
  not not_5 (not_5_out, ALUOp2);
  not not_6 (not_6_out, func3);
  not not_7 (not_7_out, func2);
  not not_8 (not_8_out, ALUOp2);
  not not_9 (not_9_out, func3);
  not not_10 (not_10_out, ALUOp2);
  not not_11 (not_11_out, ALUOp1);
  not not_12 (not_12_out, ALUOp3);
  not not_13 (not_13_out, ALUOp1);
  not not_14 (not_14_out, ALUOp0);
  not not_15 (not_15_out, ALUOp0);
  not not_16 (not_16_out, func0);
  not not_17 (not_17_out, func1);
  not not_18 (not_18_out, ALUOp2);
  not not_19 (not_19_out, ALUOp1);
  not not_20 (not_20_out, ALUOp0);
  not not_21 (not_21_out, ALUOp2);
  not not_22 (not_22_out, func3);
  not not_23 (not_23_out, func2);
  not not_24 (not_24_out, ALUOp2);
  not not_25 (not_25_out, func1);
  not not_26 (not_26_out, func0);
  not not_27 (not_27_out, ALUOp1);
  not not_28 (not_28_out, ALUOp0);
  not not_29 (not_29_out, ALUOp2);
  not not_30 (not_30_out, func2);
  not not_31 (not_31_out, ALUOp2);
  or or_1 (ALUCtl3, and_1_out, ALUOp3);
  and and_2 (and_2_out, not_1_out, not_2_out, not_3_out);
  and and_3 (and_3_out, not_4_out, not_5_out, not_6_out, not_7_out);
  and and_4 (and_4_out, not_8_out, not_9_out, func0);
  and and_5 (and_5_out, not_10_out, ALUOp0);
  and and_6 (and_6_out, not_11_out, ALUOp0);
  and and_7 (and_7_out, not_12_out, not_13_out, not_14_out);
  and and_8 (and_8_out, not_15_out, func3, not_16_out);
  and and_9 (and_9_out, ALUOp1, not_17_out);
  and and_10 (and_10_out, not_18_out, ALUOp1, ALUOp0);
  and and_11 (and_11_out, ALUOp2, not_19_out);
  and and_12 (and_12_out, ALUOp2, not_20_out);
  and and_13 (and_13_out, not_21_out, not_22_out, not_23_out);
  and and_14 (and_14_out, not_24_out, not_25_out, not_26_out);
  and and_15 (and_15_out, not_27_out, not_28_out);
  and and_16 (and_16_out, not_29_out, not_30_out, func0);
  and and_17 (and_17_out, not_31_out, ALUOp0);
  or or_2 (ALUCtl2, and_2_out, and_3_out, and_4_out, and_5_out, and_6_out);
  or or_3 (ALUCtl1, and_7_out, and_8_out, and_9_out, and_10_out, and_11_out, and_12_out);
  or or_4 (ALUCtl0, and_13_out, and_14_out, and_15_out, and_16_out, and_17_out);
endmodule

module alucontrol (
  input  [1:0] Op,
  input  [5:0] Func,
  input  [5:0] Opcode,
  input  [3:0] state,
  output [3:0] ALUCtrl
);

  wire comparator_1_eq, comparator_2_eq, comparator_3_eq, comparator_4_eq, isI, not_1_out, or_1_out;
  wire [3:0] rom_1_data, rom_2_data;

  Comparator #(.width(6)) comparator_1 (.a(Opcode), .b(6'b001100), .eq(comparator_1_eq));  // open: gt, lt
  Comparator #(.width(6)) comparator_2 (.a(Opcode), .b(6'b001000), .eq(comparator_2_eq));  // open: gt, lt
  Comparator #(.width(6)) comparator_3 (.a(Opcode), .b(6'b001101), .eq(comparator_3_eq));  // open: gt, lt
  Comparator #(.width(4)) comparator_4 (.a(state), .b(4'b0000), .eq(comparator_4_eq));  // open: gt, lt
  or or_1 (or_1_out, comparator_1_eq, comparator_2_eq, comparator_3_eq);
  not not_1 (not_1_out, comparator_4_eq);
  ROM #(.dataWidth(4)) rom_1 (.addr({Op, Func}), .data(rom_1_data));  // open: sel
  ROM #(.addrWidth(6), .dataWidth(4)) rom_2 (.addr(Opcode), .data(rom_2_data));  // open: sel
  Multiplexer #(.width(4), .enable("false")) multiplexer_1 (
    .in0(rom_1_data), .in1(rom_2_data), .out(ALUCtrl), .sel(isI));
  and and_1 (isI, or_1_out, not_1_out);

  // Other names for the same wires on the sheet: op_t[5:0] = Opcode

  // Notes on the sheet:
  //   contents of rom_1 (hex, n*v repeats v):
  //   64*3 64*4 f 0 e 29*0 3 0 4 0 6 0 5 0 0 0 2 1
  //   contents of rom_2 (hex, n*v repeats v):
  //   8*0 3 0 0 0 6
endmodule
