// Logisim project Lab 4.circ as structural Verilog: 8 circuits, main circuit Main
module Main (
);

  wire ALUSrc, and_1_out, Branch, Clock, comparator_1_eq, comparator_2_eq, comparator_3_eq, comparator_4_eq,
       comparator_5_eq, EX_ALUSrc, EX_Branch, EX_MEM_Zero_q, EX_MemRead, EX_MemWr, EX_RegWrite, isI, Jump,
       MEM_Branch, MEM_MemRead, MEM_MemWr, MEM_RegWrite, MemRead, MemWr, PCSrc, RegWrite, stall, undriven,
       undriven_4, WB_RegWrite, Zero;
  wire [1:0] EX_MemtoReg, EX_RegDst, ForwardA, ForwardB, ForwardImm, MEM_MemtoReg, MemtoReg, RegDst,
       undriven_3, WB_MemtoReg;
  wire [2:0] ALUOp, EX_ALUOp;
  wire [3:0] ALUCtl;
  wire [4:0] EX_MEM_RegDst_q, EX_rd, EX_rs, EX_rt, EX_shamt, IF_rs, IF_rt, MEM_rd, MEM_rt, multiplexer_6_out,
       undriven_2, WB_rd, WrAddr;
  wire [5:0] EX_func, EX_op, func, MEM_op;
  wire [31:0] adder_1_out, adder_2_out, ALUResult, EX_MEM_PC_q, EX_MEM_RdData2_q, ID_EX_PC_q,
       ID_EX_RdData1_q, ID_EX_RdData2_q, ID_EX_Sign_Extend_q, IF_ID_PC_q, MEM_ALUResult, MEM_WB_MemRead_q,
       MEM_WB_ReadData_q, MemData, multiplexer_1_out, multiplexer_3_out, multiplexer_4_out,
       multiplexer_5_out, PC, register_file_1_rddata1, register_file_1_rddata2, rom_1_data, shifter_2_out,
       Sign_Extend, SignExtShifted, WrData;
  wire [31:6] Instruction;

  Register #(.width(32)) u_PC (.clk(Clock));  // open: D, en, Q, clr
  // Probe on PC
  Register #(.width(32)) PC_3 (.D(multiplexer_1_out), .Q(PC), .clk(Clock));  // open: en, clr
  Multiplexer #(.width(32), .enable("false")) multiplexer_1 (
    .in0(adder_1_out), .in1(EX_MEM_PC_q), .out(multiplexer_1_out), .sel(PCSrc));
  // Probe on undriven
  Comparator #(.width(6)) comparator_1 (.a(EX_op), .b(6'b001100), .eq(comparator_1_eq));  // open: gt, lt
  Comparator #(.width(6)) comparator_2 (.a(MEM_op), .b(6'b001000), .eq(comparator_2_eq));  // open: gt, lt
  Comparator #(.width(6)) comparator_3 (.a(EX_op), .b(6'b001101), .eq(comparator_3_eq));  // open: gt, lt
  Comparator #(.width(6)) comparator_4 (.a(EX_op), .b(6'b001010), .eq(comparator_4_eq));  // open: gt, lt
  Clock u_Clock (.out(Clock));
  Adder #(.width(32)) adder_1 (.a(PC), .b(32'h4), .out(adder_1_out));  // open: cin, cout
  ROM #(.dataWidth(32)) rom_1 (
    .addr(PC[9:2]), .data({rom_1_data[31:21], IF_rs, IF_rt, rom_1_data[10:0]}));  // open: sel
  Main_Control_Unit main_control_unit_1 (
    .op(Instruction[31:26]), .RegDst(RegDst), .ALUSrc(ALUSrc), .MemtoReg(MemtoReg), .RegWrite(RegWrite),
    .MemRead(MemRead), .MemWr(MemWr), .Branch(Branch), .ALUOp(ALUOp));
  ALU_Control_Unit alu_control_unit_1 (.ALUOp(EX_ALUOp), .func(EX_func), .ALUCtl(ALUCtl));
  // Probe on EX_func
  Hazard_Detection_Unit hazard_detection_unit_1 (
    .EX_rt(EX_rt), .out(stall), .ID_rs(IF_rs), .ID_rt(undriven_2), .EX_MemRead(EX_MemRead));
  Register #(.width(32)) IF_ID_PC (.D(adder_1_out), .Q(IF_ID_PC_q), .clk(Clock));  // open: en, clr
  // Probe on {rom_1_data[31:21], IF_rs, IF_rt, rom_1_data[10:0]}
  Register #(.width(32)) IF_ID_Instr (
    .D({rom_1_data[31:21], IF_rs, IF_rt, rom_1_data[10:0]}), .Q({Instruction, func}), .clk(Clock));  // open: en, clr
  or or_1 (isI, comparator_1_eq, comparator_2_eq, comparator_3_eq, comparator_4_eq);
  // Probe on func
  // Probe on Instruction[31:26]
  // Probe on Instruction[25:21]
  // Probe on EX_func
  // Probe on register_file_1_rddata1
  Register_File register_file_1 (
    .WrAddr(WrAddr), .WrData(WrData), .WrReg(WB_RegWrite), .RdAddr1(Instruction[25:21]),
    .RdAddr2(Instruction[20:16]), .RdData1(register_file_1_rddata1), .RdData2(register_file_1_rddata2),
    .Clock(Clock));
  // Probe on register_file_1_rddata2
  // Probe on Sign_Extend
  // Probe on Instruction[20:16]
  // Probe on Instruction[15:11]
  // Probe on {Instruction[15:6], func}
  // Probe on WrData
  Register #(.width(32)) ID_EX_PC (.D(IF_ID_PC_q), .Q(ID_EX_PC_q), .clk(Clock));  // open: en, clr
  Register #(.width(32)) ID_EX_RdData1 (
    .D(register_file_1_rddata1), .Q(ID_EX_RdData1_q), .clk(Clock));  // open: en, clr
  Register #(.width(32)) ID_EX_RdData2 (
    .D(register_file_1_rddata2), .Q(ID_EX_RdData2_q), .clk(Clock));  // open: en, clr
  Register #(.width(32)) ID_EX_Sign_Extend (.D(Sign_Extend), .Q(ID_EX_Sign_Extend_q), .clk(Clock));  // open: en, clr
  Register #(.width(5)) ID_EX_rt (.D(Instruction[20:16]), .Q(EX_rt), .clk(Clock));  // open: en, clr
  // Probe on EX_rt
  Register #(.width(5)) ID_EX_rd (.D(Instruction[15:11]), .Q(EX_rd), .clk(Clock));  // open: en, clr
  Register #(.width(6)) ID_EX_Green (
    .D({ALUOp, RegDst, ALUSrc}), .Q({EX_ALUOp, EX_RegDst, EX_ALUSrc}), .clk(Clock));  // open: en, clr
  Register #(.width(2)) ID_EX_Red (.D({MemWr, Branch}), .Q({EX_MemWr, EX_Branch}), .clk(Clock));  // open: en, clr
  Register #(.width(3)) ID_EX_Blue (
    .D({RegWrite, MemtoReg}), .Q({EX_RegWrite, EX_MemtoReg}), .clk(Clock));  // open: en, clr
  Register #(.width(5)) ID_EX_shamt (.D(Instruction[10:6]), .Q(EX_shamt), .clk(Clock));  // open: en, clr
  Register #(.width(6)) ID_EX_func (.D(func), .Q(EX_func), .clk(Clock));  // open: en, clr
  Register #(.width(5)) ID_EX_rs (.D(Instruction[25:21]), .Q(EX_rs), .clk(Clock));  // open: en, clr
  Register #(.width(1)) ID_EX_rs_2 (.D(MemRead), .Q(EX_MemRead), .clk(Clock));  // open: en, clr
  Register #(.width(6)) ID_EX_func_2 (.D(Instruction[31:26]), .Q(EX_op), .clk(Clock));  // open: en, clr
  // Probe on Sign_Extend
  assign Sign_Extend = {{16{Instruction[15]}}, {Instruction[15:6], func}};  // Bit_Extender bit_extender_1
  // Probe on MEM_ALUResult
  // Probe on ForwardB
  // Probe on MEM_ALUResult
  Multiplexer #(.width(2), .enable("false")) multiplexer_2 (
    .in0(undriven_3), .in1(2'b00), .out(ForwardImm));  // open: sel
  Comparator #(.width(5)) comparator_5 (.a(Instruction[20:16]), .b(EX_rt), .eq(comparator_5_eq));  // open: gt, lt
  // Probe on ForwardA
  Multiplexer #(.select(2), .width(32), .enable("false")) multiplexer_3 (
    .in0(ID_EX_RdData1_q), .in1(WrData), .in2(MEM_ALUResult), .in3(MEM_ALUResult), .out(multiplexer_3_out),
    .sel(ForwardA));
  Multiplexer #(.select(2), .width(32), .enable("false")) multiplexer_4 (
    .in0(ID_EX_RdData2_q), .in1(WrData), .in2(MEM_ALUResult), .in3(MEM_ALUResult), .out(multiplexer_4_out),
    .sel(ForwardB));
  // Probe on ID_EX_Sign_Extend_q
  and and_1 (and_1_out, isI, comparator_5_eq);
  Comparator #(.width(6)) comparator_6 (.a(Instruction[31:26]), .b(6'b000010), .eq(Jump));  // open: gt, lt
  Shifter #(.width(32)) shifter_1 (.in(Sign_Extend), .\dist (5'b00010), .out(SignExtShifted));
  // Probe on ALUCtl
  Multiplexer #(.width(32), .enable("false")) multiplexer_5 (
    .in0(multiplexer_4_out), .in1(ID_EX_Sign_Extend_q), .out(multiplexer_5_out), .sel(EX_ALUSrc));
  // Probe on multiplexer_5_out
  Multiplexer #(.select(2), .width(5), .enable("false")) multiplexer_6 (
    .in0(EX_rt), .in1(EX_rd), .out(multiplexer_6_out), .sel(EX_RegDst));  // open: in2, in3
  // Probe on undriven_4
  Forwarding_Unit forwarding_unit_1 (
    .EX_rt(EX_rt), .EX_rs(EX_rs), .MEM_rd(MEM_rd), .WB_rd(WB_rd), .MEM_RegWrite(MEM_RegWrite),
    .WB_RegWrite(WB_RegWrite), .ForwardB(ForwardB), .EX_op_2(MEM_op), .ForwardA(ForwardA),
    .EX_rt_2(Instruction[20:16]), .EX_op(EX_op));
  // Probe on multiplexer_3_out
  Shifter #(.width(32)) shifter_2 (.in(ID_EX_Sign_Extend_q), .\dist (5'b00010), .out(shifter_2_out));
  ALU alu_1 (
    .ALUCtl(ALUCtl), .A(multiplexer_3_out), .B(multiplexer_5_out), .ALUResult(ALUResult), .Zero(Zero),
    .Shamt(EX_shamt));  // open: Overflow
  // Probe on EX_shamt
  // Probe on multiplexer_4_out
  Register #(.width(5)) EX_MEM_rd (.D(EX_rd), .Q(MEM_rd), .clk(Clock));  // open: en, clr
  Register #(.width(3)) EX_MEM_Red (
    .D({EX_MemWr, EX_MemRead, EX_Branch}), .Q({MEM_MemWr, MEM_MemRead, MEM_Branch}), .clk(Clock));  // open: en, clr
  Register #(.width(3)) EX_MEM_Blue (
    .D({EX_RegWrite, EX_MemtoReg}), .Q({MEM_RegWrite, MEM_MemtoReg}), .clk(Clock));  // open: en, clr
  Adder #(.width(32)) adder_2 (.a(ID_EX_PC_q), .b(shifter_2_out), .out(adder_2_out));  // open: cin, cout
  // Probe on ALUResult
  // Probe on EX_rt
  Register #(.width(32)) EX_MEM_PC (.D(adder_2_out), .Q(EX_MEM_PC_q), .clk(Clock));  // open: en, clr
  Register #(.width(32)) EX_MEM_ALUResult (.D(ALUResult), .Q(MEM_ALUResult), .clk(Clock));  // open: en, clr
  Register #(.width(32)) EX_MEM_RdData2 (.D(multiplexer_4_out), .Q(EX_MEM_RdData2_q), .clk(Clock));  // open: en, clr
  Register #(.width(5)) EX_MEM_RegDst (.D(multiplexer_6_out), .Q(EX_MEM_RegDst_q), .clk(Clock));  // open: en, clr
  Register #(.width(5)) ID_EX_rt_2 (.D(EX_rt), .Q(MEM_rt), .clk(Clock));  // open: en, clr
  // Probe on MEM_rt
  Register #(.width(6)) ID_EX_func_3 (.D(EX_op), .Q(MEM_op), .clk(Clock));  // open: en, clr
  // Probe on MEM_ALUResult
  // Probe on MEM_ALUResult[9:2]
  Register #(.width(1)) EX_MEM_Zero (.D(Zero), .Q(EX_MEM_Zero_q), .clk(Clock));  // open: en, clr
  // Probe on EX_MEM_RdData2_q
  and and_2 (PCSrc, MEM_Branch, EX_MEM_Zero_q);
  RAM #(.dataWidth(32), .bus("separate")) ram_1 (
    .addr(MEM_ALUResult[9:2]), .din(EX_MEM_RdData2_q), .data(MemData), .str(MEM_MemWr), .clk(Clock),
    .ld(MEM_MemRead));  // open: sel, clr
  // Probe on EX_MEM_RegDst_q
  Register #(.width(5)) MEM_WB_rd (.D(MEM_rd), .Q(WB_rd), .clk(Clock));  // open: en, clr
  Register #(.width(3)) EX_MEM_Blue_2 (
    .D({MEM_RegWrite, MEM_MemtoReg}), .Q({WB_RegWrite, WB_MemtoReg}), .clk(Clock));  // open: en, clr
  // Probe on MemData
  // Probe on MEM_ALUResult
  Register #(.width(32)) MEM_WB_PC (.clk(Clock));  // open: D, en, Q, clr
  Register #(.width(32)) MEM_WB_ReadData (.D(MemData), .Q(MEM_WB_ReadData_q), .clk(Clock));  // open: en, clr
  Register #(.width(32)) MEM_WB_MemRead (.D(MEM_ALUResult), .Q(MEM_WB_MemRead_q), .clk(Clock));  // open: en, clr
  Register #(.width(5)) MEM_WB_RegDst (.D(EX_MEM_RegDst_q), .Q(WrAddr), .clk(Clock));  // open: en, clr
  // Probe on MEM_WB_ReadData_q
  // Probe on MEM_WB_MemRead_q
  Multiplexer #(.select(2), .width(32), .enable("false")) multiplexer_7 (
    .in0(MEM_WB_MemRead_q), .in1(MEM_WB_ReadData_q), .out(WrData), .sel(WB_MemtoReg));  // open: in2, in3
  // Probe on WB_MemtoReg
  // Probe on PC
  // Probe on Branch
  // Probe on nothing
  // Probe on nothing
  // Probe on nothing
  // Probe on RegWrite
  // Probe on WrAddr
  // Probe on WrData
  // Probe on MemWr
  // Probe on MemData
  // Probe on MEM_MemRead

  // Other names for the same wires on the sheet: Instruction[5:0] = func; shamt[4:0] = Instruction[10:6];
  //   rd[4:0] = Instruction[15:11]; rt[4:0] = Instruction[20:16]; rs[4:0] = Instruction[25:21];
  //   op[5:0] = Instruction[31:26]

  // Notes on the sheet:
  //   andi
  //   addi
  //   ori
  //   slti
  //   contents of rom_1 (hex, n*v repeats v):
  //   20010001 5*210820 ac010000 8c020000 211824 ac630000 8c640000 ac640004
  //   Main Control Unit
  //   ALU Control Unit
  //   Hazard Detection Unit
  //   Sign extend for mux input 2, then shift it for mux input 3
  //   forwarding unit
endmodule

module ALU (
  input  [3:0] ALUCtl,
  input  [31:0] A,
  input  [31:0] B,
  input  [4:0] Shamt,
  output [31:0] ALUResult,
  output Zero,
  output Overflow
);

  wire comparator_1_lt, comparator_2_lt, comparator_3_eq, comparator_4_eq, or_2_out;
  wire [31:0] ADD, AND, NOR, OR, SLL, SLT, SLTU, SRL, SUB, XOR;

  assign XOR = A ^ B;  // XOR_Gate xor_1, 32 bits wide
  Adder #(.width(32)) adder_1 (.a(A), .b(B), .out(ADD));  // open: cin, cout
  Subtractor #(.width(32)) subtractor_1 (.a(A), .b(B), .out(SUB));  // open: bin, bout
  assign AND = A & B;  // AND_Gate and_1, 32 bits wide
  assign OR = A | B;  // OR_Gate or_1, 32 bits wide
  assign NOR = ~(A | B);  // NOR_Gate nor_1, 32 bits wide
  Comparator #(.width(32)) comparator_1 (.a(A), .b(B), .lt(comparator_1_lt));  // open: gt, eq
  assign SLT = {{31{1'b0}}, comparator_1_lt};  // Bit_Extender bit_extender_1
  Shifter #(.width(32)) shifter_1 (.in(B), .\dist (Shamt), .out(SLL));
  Shifter #(.width(32), .shift("lr")) shifter_2 (.in(B), .\dist (Shamt), .out(SRL));
  Comparator #(.width(32), .mode("unsigned")) comparator_2 (.a(A), .b(B), .lt(comparator_2_lt));  // open: gt, eq
  assign SLTU = {{31{1'b0}}, comparator_2_lt};  // Bit_Extender bit_extender_2
  Multiplexer #(.select(4), .width(32), .enable("false")) multiplexer_1 (
    .in0(XOR), .in1(SLTU), .in2(SLT), .in3(AND), .in4(NOR), .in5(SUB), .in6(OR), .in7(ADD), .in8(SRL),
    .in9(SLL), .out(ALUResult), .sel(ALUCtl));  // open: in10, in11, in12, in13, in14, in15
  Comparator #(.width(4)) comparator_3 (.a(4'b0111), .b(ALUCtl), .eq(comparator_3_eq));  // open: gt, lt
  Comparator #(.width(4)) comparator_4 (.a(ALUCtl), .b(4'b0101), .eq(comparator_4_eq));  // open: gt, lt
  Overflow_Unit overflow_unit_1 (
    .Add(comparator_3_eq), .Sub(comparator_4_eq), .ASign(A[31]), .BSign(B[31]), .ResultSign(ALUResult[31]),
    .Overflow(Overflow));
  or or_2 (or_2_out, ALUResult[0], ALUResult[1], ALUResult[2], ALUResult[3], ALUResult[4], ALUResult[5], ALUResult[6], ALUResult[7], ALUResult[8], ALUResult[9], ALUResult[10], ALUResult[11], ALUResult[12], ALUResult[13], ALUResult[14], ALUResult[15], ALUResult[16], ALUResult[17], ALUResult[18], ALUResult[19], ALUResult[20], ALUResult[21], ALUResult[22], ALUResult[23], ALUResult[24], ALUResult[25], ALUResult[26], ALUResult[27], ALUResult[28], ALUResult[29], ALUResult[30], ALUResult[31]);
  not not_1 (Zero, or_2_out);

  // Other names for the same wires on the sheet: ASign = A[31]; ResultSign = ALUResult[31]; BSign = B[31]

  // Notes on the sheet:
  //   ALUCtl for ADD on top port
  //   ALUCtl for SUB on second port
endmodule

module Register_File (
  input  [4:0] WrAddr,
  input  [31:0] WrData,
  input  WrReg,
  input  [4:0] RdAddr1,
  input  [4:0] RdAddr2,
  input  Clock,
  output [31:0] RdData1,
  output [31:0] RdData2
);

  wire and_1_out, and_2_out, comparator_1_eq, comparator_2_eq, comparator_3_eq, comparator_4_eq, not_1_out,
       not_2_out, WrReg0, WrReg1, WrReg2, WrReg3, WrReg4, WrReg5, WrReg6, WrReg7, WrReg8, WrReg9, WrReg10,
       WrReg11, WrReg12, WrReg13, WrReg14, WrReg15, WrReg16, WrReg17, WrReg18, WrReg19, WrReg20, WrReg21,
       WrReg22, WrReg23, WrReg24, WrReg25, WrReg26, WrReg27, WrReg28, WrReg29, WrReg30, WrReg31;
  wire [31:0] multiplexer_1_out, multiplexer_2_out, RegData1, RegData2, RegData3, RegData4, RegData5,
       RegData6, RegData7, RegData8, RegData9, RegData10, RegData11, RegData12, RegData13, RegData14,
       RegData15, RegData16, RegData17, RegData18, RegData19, RegData20, RegData21, RegData22, RegData23,
       RegData24, RegData25, RegData26, RegData27, RegData28, RegData29, RegData30, RegData31;

  Demultiplexer #(.select(5), .enable("false")) demultiplexer_1 (
    .out0(WrReg0), .out1(WrReg1), .out2(WrReg2), .out3(WrReg3), .out4(WrReg4), .out5(WrReg5), .out6(WrReg6),
    .out7(WrReg7), .out8(WrReg8), .out9(WrReg9), .out10(WrReg10), .out11(WrReg11), .out12(WrReg12),
    .out13(WrReg13), .out14(WrReg14), .out15(WrReg15), .out16(WrReg16), .out17(WrReg17), .out18(WrReg18),
    .out19(WrReg19), .out20(WrReg20), .out21(WrReg21), .out22(WrReg22), .out23(WrReg23), .out24(WrReg24),
    .out25(WrReg25), .out26(WrReg26), .out27(WrReg27), .out28(WrReg28), .out29(WrReg29), .out30(WrReg30),
    .out31(WrReg31), .in(WrReg), .sel(WrAddr));
  // Probe on RegData4
  Register #(.width(32)) Reg4 (.D(WrData), .en(WrReg4), .Q(RegData4), .clk(Clock));  // open: clr
  // Probe on RegData8
  Register #(.width(32)) Reg8 (.D(WrData), .en(WrReg8), .Q(RegData8), .clk(Clock));  // open: clr
  // Probe on RegData12
  Register #(.width(32)) Reg12 (.D(WrData), .en(WrReg12), .Q(RegData12), .clk(Clock));  // open: clr
  // Probe on RegData16
  Register #(.width(32)) Reg16 (.D(WrData), .en(WrReg16), .Q(RegData16), .clk(Clock));  // open: clr
  // Probe on RegData20
  Register #(.width(32)) Reg20 (.D(WrData), .en(WrReg20), .Q(RegData20), .clk(Clock));  // open: clr
  // Probe on RegData24
  Register #(.width(32)) Reg24 (.D(WrData), .en(WrReg24), .Q(RegData24), .clk(Clock));  // open: clr
  // Probe on RegData28
  Register #(.width(32)) Reg28 (.D(WrData), .en(WrReg28), .Q(RegData28), .clk(Clock));  // open: clr
  Register #(.width(32)) Reg1 (.D(WrData), .en(WrReg1), .Q(RegData1), .clk(Clock));  // open: clr
  Register #(.width(32)) Reg5 (.D(WrData), .en(WrReg5), .Q(RegData5), .clk(Clock));  // open: clr
  Register #(.width(32)) Reg9 (.D(WrData), .en(WrReg9), .Q(RegData9), .clk(Clock));  // open: clr
  Register #(.width(32)) Reg13 (.D(WrData), .en(WrReg13), .Q(RegData13), .clk(Clock));  // open: clr
  Register #(.width(32)) Reg17 (.D(WrData), .en(WrReg17), .Q(RegData17), .clk(Clock));  // open: clr
  Register #(.width(32)) Reg21 (.D(WrData), .en(WrReg21), .Q(RegData21), .clk(Clock));  // open: clr
  Register #(.width(32)) Reg25 (.D(WrData), .en(WrReg25), .Q(RegData25), .clk(Clock));  // open: clr
  Register #(.width(32)) Reg29 (.D(WrData), .en(WrReg29), .Q(RegData29), .clk(Clock));  // open: clr
  // Probe on RegData1
  // Probe on RegData5
  // Probe on RegData9
  // Probe on RegData13
  // Probe on RegData17
  // Probe on RegData21
  // Probe on RegData25
  // Probe on RegData29
  // Probe on RegData2
  Register #(.width(32)) Reg2 (.D(WrData), .en(WrReg2), .Q(RegData2), .clk(Clock));  // open: clr
  // Probe on RegData6
  Register #(.width(32)) Reg6 (.D(WrData), .en(WrReg6), .Q(RegData6), .clk(Clock));  // open: clr
  // Probe on RegData10
  Register #(.width(32)) Reg10 (.D(WrData), .en(WrReg10), .Q(RegData10), .clk(Clock));  // open: clr
  // Probe on RegData14
  Register #(.width(32)) Reg14 (.D(WrData), .en(WrReg14), .Q(RegData14), .clk(Clock));  // open: clr
  // Probe on RegData18
  Register #(.width(32)) Reg18 (.D(WrData), .en(WrReg18), .Q(RegData18), .clk(Clock));  // open: clr
  // Probe on RegData22
  Register #(.width(32)) Reg22 (.D(WrData), .en(WrReg22), .Q(RegData22), .clk(Clock));  // open: clr
  // Probe on RegData26
  Register #(.width(32)) Reg26 (.D(WrData), .en(WrReg26), .Q(RegData26), .clk(Clock));  // open: clr
  // Probe on RegData30
  Register #(.width(32)) Reg30 (.D(WrData), .en(WrReg30), .Q(RegData30), .clk(Clock));  // open: clr
  // Probe on RegData3
  Register #(.width(32)) Reg3 (.D(WrData), .en(WrReg3), .Q(RegData3), .clk(Clock));  // open: clr
  // Probe on RegData7
  Register #(.width(32)) Reg7 (.D(WrData), .en(WrReg7), .Q(RegData7), .clk(Clock));  // open: clr
  // Probe on RegData11
  Register #(.width(32)) Reg11 (.D(WrData), .en(WrReg11), .Q(RegData11), .clk(Clock));  // open: clr
  // Probe on RegData15
  Register #(.width(32)) Reg15 (.D(WrData), .en(WrReg15), .Q(RegData15), .clk(Clock));  // open: clr
  // Probe on RegData19
  Register #(.width(32)) Reg19 (.D(WrData), .en(WrReg19), .Q(RegData19), .clk(Clock));  // open: clr
  // Probe on RegData23
  Register #(.width(32)) Reg23 (.D(WrData), .en(WrReg23), .Q(RegData23), .clk(Clock));  // open: clr
  // Probe on RegData27
  Register #(.width(32)) Reg27 (.D(WrData), .en(WrReg27), .Q(RegData27), .clk(Clock));  // open: clr
  // Probe on RegData31
  Register #(.width(32)) Reg31 (.D(WrData), .en(WrReg31), .Q(RegData31), .clk(Clock));  // open: clr
  Multiplexer #(.select(5), .width(32), .enable("false")) multiplexer_1 (
    .in0({32{1'b0}}), .in1(RegData1), .in2(RegData2), .in3(RegData3), .in4(RegData4), .in5(RegData5),
    .in6(RegData6), .in7(RegData7), .in8(RegData8), .in9(RegData9), .in10(RegData10), .in11(RegData11),
    .in12(RegData12), .in13(RegData13), .in14(RegData14), .in15(RegData15), .in16(RegData16),
    .in17(RegData17), .in18(RegData18), .in19(RegData19), .in20(RegData20), .in21(RegData21),
    .in22(RegData22), .in23(RegData23), .in24(RegData24), .in25(RegData25), .in26(RegData26),
    .in27(RegData27), .in28(RegData28), .in29(RegData29), .in30(RegData30), .in31(RegData31),
    .out(multiplexer_1_out), .sel(RdAddr1));
  Multiplexer #(.select(5), .width(32), .enable("false")) multiplexer_2 (
    .in0({32{1'b0}}), .in1(RegData1), .in2(RegData2), .in3(RegData3), .in4(RegData4), .in5(RegData5),
    .in6(RegData6), .in7(RegData7), .in8(RegData8), .in9(RegData9), .in10(RegData10), .in11(RegData11),
    .in12(RegData12), .in13(RegData13), .in14(RegData14), .in15(RegData15), .in16(RegData16),
    .in17(RegData17), .in18(RegData18), .in19(RegData19), .in20(RegData20), .in21(RegData21),
    .in22(RegData22), .in23(RegData23), .in24(RegData24), .in25(RegData25), .in26(RegData26),
    .in27(RegData27), .in28(RegData28), .in29(RegData29), .in30(RegData30), .in31(RegData31),
    .out(multiplexer_2_out), .sel(RdAddr2));
  Multiplexer #(.width(32), .enable("false")) multiplexer_3 (
    .in0(multiplexer_1_out), .in1(WrData), .out(RdData1), .sel(and_1_out));
  Comparator #(.width(5), .mode("unsigned")) comparator_1 (
    .a(WrAddr), .b(RdAddr2), .eq(comparator_1_eq));  // open: gt, lt
  Multiplexer #(.width(32), .enable("false")) multiplexer_4 (
    .in0(multiplexer_2_out), .in1(WrData), .out(RdData2), .sel(and_2_out));
  Comparator #(.width(5), .mode("unsigned")) comparator_2 (
    .a(WrAddr), .b(RdAddr1), .eq(comparator_2_eq));  // open: gt, lt
  and and_1 (and_1_out, comparator_2_eq, WrReg, not_1_out);
  and and_2 (and_2_out, comparator_1_eq, WrReg, not_2_out);
  Comparator #(.width(5), .mode("unsigned")) comparator_3 (
    .a(WrAddr), .b({5{1'b0}}), .eq(comparator_3_eq));  // open: gt, lt
  not not_1 (not_1_out, comparator_3_eq);
  Comparator #(.width(5), .mode("unsigned")) comparator_4 (
    .a(WrAddr), .b({5{1'b0}}), .eq(comparator_4_eq));  // open: gt, lt
  not not_2 (not_2_out, comparator_4_eq);
endmodule

module Overflow_Unit (
  input  Add,
  input  Sub,
  input  ASign,
  input  BSign,
  input  ResultSign,
  output Overflow
);

  wire and_1_out, and_2_out, or_1_out, xnor_1_out, xor_1_out, xor_2_out;

  xnor xnor_1 (xnor_1_out, ASign, BSign);
  xor xor_1 (xor_1_out, ASign, BSign);
  and and_1 (and_1_out, xnor_1_out, Add);
  and and_2 (and_2_out, xor_1_out, Sub);
  or or_1 (or_1_out, and_1_out, and_2_out);
  xor xor_2 (xor_2_out, ResultSign, ASign);
  and and_3 (Overflow, or_1_out, xor_2_out);

  // Notes on the sheet:
  //   Overflow occurs when doing addition and sign(A) == sign(B) && sign(result) != sign(A)
  //   Or
  //   Overflow occurs when doing subtraction and sign(A) != sign(B) && sign(result) != sign(A)
endmodule

module ALU_Control_Unit (
  input  [2:0] ALUOp,
  input  [5:0] func,
  output [3:0] ALUCtl
);

  ROM #(.addrWidth(9), .dataWidth(4)) rom_1 (.addr({ALUOp, func}), .data(ALUCtl));  // open: sel

  // Notes on the sheet:
  //   contents of rom_1 (hex, n*v repeats v):
  //   64*7 64*5 9 0 8 29*0 7 0 5 0 3 6 0 4 0 0 2 1 20*0 64*7 64*3 64*6 64*2
endmodule

module Main_Control_Unit (
  input  [5:0] op,
  output [1:0] RegDst,
  output ALUSrc,
  output [1:0] MemtoReg,
  output RegWrite,
  output MemRead,
  output MemWr,
  output Branch,
  output [2:0] ALUOp
);

  ROM #(.addrWidth(6), .dataWidth(12)) rom_1 (
    .addr(op), .data({RegDst, ALUSrc, MemtoReg, RegWrite, MemRead, MemWr, Branch, ALUOp}));  // open: sel

  // Notes on the sheet:
  //   contents of rom_1 (hex, n*v repeats v):
  //   442 0 0 0 9 0 0 0 243 0 246 0 244 245 21*0 2e0 7*0 210
endmodule

module Forwarding_Unit (
  input  [4:0] EX_rt,
  input  [4:0] MEM_rd,
  input  [4:0] EX_rs,
  input  [4:0] WB_rd,
  input  MEM_RegWrite,
  input  WB_RegWrite,
  input  [5:0] EX_op,
  input  [5:0] EX_op_2,
  input  [4:0] EX_rt_2,
  output [1:0] ForwardB,
  output [1:0] ForwardA
);

  wire and_2_out, and_3_out, and_4_out, and_5_out, comparator_1_eq, comparator_2_eq, comparator_3_eq,
       comparator_4_eq, comparator_5_eq, comparator_6_eq, comparator_7_eq, comparator_8_eq, comparator_9_eq,
       comparator_10_eq, comparator_11_eq, comparator_12_eq, comparator_13_eq, comparator_14_eq,
       comparator_15_eq, comparator_16_eq, comparator_17_eq, comparator_18_eq, comparator_19_eq,
       comparator_20_eq, comparator_21_eq, comparator_22_eq, comparator_23_eq, corrected_A, corrected_B,
       ForwardImm, isI, lw, sw;

  Comparator #(.width(5)) comparator_1 (.a(MEM_rd), .b({5{1'b0}}), .eq(comparator_1_eq));  // open: gt, lt
  Comparator #(.width(5)) comparator_2 (.a(MEM_rd), .b(EX_rs), .eq(comparator_2_eq));  // open: gt, lt
  and and_1 (corrected_A, MEM_RegWrite, ~comparator_1_eq, ~comparator_2_eq);  // AND_Gate
  or or_1 (ForwardB[1], lw, and_2_out, ForwardImm, sw);
  and and_2 (and_2_out, MEM_RegWrite, ~comparator_3_eq, comparator_4_eq);  // AND_Gate
  Comparator #(.width(5)) comparator_3 (.a(MEM_rd), .b({5{1'b0}}), .eq(comparator_3_eq));  // open: gt, lt
  Comparator #(.width(5)) comparator_4 (.a(MEM_rd), .b(EX_rt), .eq(comparator_4_eq));  // open: gt, lt
  Comparator #(.width(6)) comparator_5 (.a(EX_op_2), .b(6'b001100), .eq(comparator_5_eq));  // open: gt, lt
  Comparator #(.width(6)) comparator_6 (.a(EX_op_2), .b(6'b001000), .eq(comparator_6_eq));  // open: gt, lt
  Comparator #(.width(6)) comparator_7 (.a(EX_op_2), .b(6'b001101), .eq(comparator_7_eq));  // open: gt, lt
  Comparator #(.width(6)) comparator_8 (.a(EX_op_2), .b(6'b001010), .eq(comparator_8_eq));  // open: gt, lt
  or or_2 (ForwardB[0], and_3_out, sw, ForwardImm);
  and and_3 (and_3_out, WB_RegWrite, comparator_9_eq, ~corrected_B, ~comparator_11_eq);  // AND_Gate
  Comparator #(.width(5)) comparator_9 (.a(WB_rd), .b(EX_rt), .eq(comparator_9_eq));  // open: gt, lt
  Comparator #(.width(5)) comparator_10 (.a(EX_rt), .b(MEM_rd), .eq(comparator_10_eq));  // open: gt, lt
  Comparator #(.width(5)) comparator_11 (.a(WB_rd), .b({5{1'b0}}), .eq(comparator_11_eq));  // open: gt, lt
  or or_3 (isI, comparator_5_eq, comparator_6_eq, comparator_7_eq, comparator_8_eq);
  Comparator #(.width(5)) comparator_12 (.a(EX_rt_2), .b(EX_rt), .eq(comparator_12_eq));  // open: gt, lt
  or or_4 (ForwardA[0], and_4_out, sw, ForwardImm);
  and and_4 (and_4_out, WB_RegWrite, comparator_13_eq, ~corrected_A, ~comparator_15_eq);  // AND_Gate
  Comparator #(.width(5)) comparator_13 (.a(EX_rs), .b(WB_rd), .eq(comparator_13_eq));  // open: gt, lt
  Comparator #(.width(5)) comparator_14 (.a(EX_rs), .b(MEM_rd), .eq(comparator_14_eq));  // open: gt, lt
  Comparator #(.width(5)) comparator_15 (.a(WB_rd), .b({5{1'b0}}), .eq(comparator_15_eq));  // open: gt, lt
  or or_5 (ForwardA[1], sw, and_5_out, ForwardImm, lw);
  and and_5 (and_5_out, MEM_RegWrite, ~comparator_16_eq, comparator_17_eq);  // AND_Gate
  Comparator #(.width(5)) comparator_16 (.a(MEM_rd), .b({5{1'b0}}), .eq(comparator_16_eq));  // open: gt, lt
  Comparator #(.width(5)) comparator_17 (.a(MEM_rd), .b(EX_rs), .eq(comparator_17_eq));  // open: gt, lt
  and and_6 (ForwardImm, isI, comparator_12_eq);
  Comparator #(.width(5)) comparator_18 (.a(MEM_rd), .b({5{1'b0}}), .eq(comparator_18_eq));  // open: gt, lt
  Comparator #(.width(5)) comparator_19 (.a(MEM_rd), .b(EX_rt), .eq(comparator_19_eq));  // open: gt, lt
  Comparator #(.width(6)) comparator_20 (.a(EX_op), .b(6'b101011), .eq(comparator_20_eq));  // open: gt, lt
  Comparator #(.width(5)) comparator_21 (.a(EX_rt_2), .b(EX_rt), .eq(comparator_21_eq));  // open: gt, lt
  and and_7 (sw, comparator_20_eq, comparator_21_eq);
  and and_8 (corrected_B, MEM_RegWrite, ~comparator_18_eq, ~comparator_19_eq);  // AND_Gate
  Comparator #(.width(6)) comparator_22 (.a(EX_op), .b(6'b100011), .eq(comparator_22_eq));  // open: gt, lt
  Comparator #(.width(5)) comparator_23 (.a(MEM_rd), .b(EX_rs), .eq(comparator_23_eq));  // open: gt, lt
  and and_9 (lw, comparator_22_eq, comparator_23_eq);

  // Other names for the same wires on the sheet: TrueA = ForwardA[1]; TrueB = ForwardB[1]; MEM_op[5:0] = EX_op_2;
  //   rt[4:0] = EX_rt_2

  // Notes on the sheet:
  //   andi
  //   addi
  //   ori
  //   slti
  //   EX/MEM Hazard
  //   lw
  //   MEM/WB Hazard
  //   lw
endmodule

module Hazard_Detection_Unit (
  input  [4:0] EX_rt,
  input  [4:0] ID_rs,
  input  [4:0] ID_rt,
  input  EX_MemRead,
  output out
);

  wire comparator_1_eq, comparator_2_eq, comparator_3_eq, or_1_out;

  Comparator #(.width(5)) comparator_1 (.a(ID_rt), .b(EX_rt), .eq(comparator_1_eq));  // open: gt, lt
  Comparator #(.width(5)) comparator_2 (.a(ID_rs), .b(EX_rt), .eq(comparator_2_eq));  // open: gt, lt
  or or_1 (or_1_out, comparator_2_eq, comparator_1_eq);
  Comparator #(.width(5)) comparator_3 (.a(EX_rt), .b({5{1'b0}}), .eq(comparator_3_eq));  // open: gt, lt
  and and_1 (out, ~comparator_3_eq, or_1_out);  // AND_Gate
endmodule
